// Logisim project Lab1.circ as structural Verilog: 17 circuits, main circuit main
module main (
  input  ReadEnable,
  input  Reset
);

  wire clock_1_out, keyboard_1_avail;
  wire [6:0] keyboard_1_data;

  Clock clock_1 (.out(clock_1_out));
  Keyboard keyboard_1 (
    .clk(clock_1_out), .re(ReadEnable), .clr(Reset), .avail(keyboard_1_avail), .data(keyboard_1_data));
  LED Available (.in(keyboard_1_avail));
  Circuito circuito_1 (
    .RESET(Reset), .AVAILABLE(keyboard_1_avail), .DATAINPUT(keyboard_1_data));  // open: COLUMNDISPLAY
endmodule

module pruebaram (
  output [6:0] out_1
);

  wire and_1_out, and_2_out, and_3_out, AVAILABLE, clock_1_out, clock_2_out, KBDENABLE, not_1_out,
       NOTAVAILABLE, or_2_out, or_4_out, RAMCLK, RESETRAMADR, RESETROMCOUNTER, ROMCOUNTERFULLCYCLE,
       SHOWMESSAGE, WRITINGCLOCK_out;
  wire [2:0] BTNSIGNALS, contadora6_1_out_4;
  wire [6:0] KDBDATA, ramaddress_1_out_3, rom_1_data;
  wire [9:0] romaddress_1_out_3;

  Button ResetBtn (.out(BTNSIGNALS[0]));
  not not_1 (not_1_out, KBDENABLE);
  Clock clock_1 (.out(clock_1_out));
  Keyboard keyboard_1 (.clk(clock_1_out), .re(KBDENABLE), .clr(BTNSIGNALS[0]), .avail(AVAILABLE), .data(KDBDATA));
  not not_2 (NOTAVAILABLE, AVAILABLE);
  or or_1 (RESETRAMADR, BTNSIGNALS[0], BTNSIGNALS[2]);
  or or_2 (or_2_out, RESETRAMADR, not_1_out);
  Button LoadMessage (.out(BTNSIGNALS[1]));
  LED u_Available (.in(AVAILABLE));
  Button u_ShowMessage (.out(BTNSIGNALS[2]));
  RamAddress ramaddress_1 (.RESET(or_2_out), .CLK(RAMCLK), .out_3(ramaddress_1_out_3));
  and and_1 (and_1_out, AVAILABLE, KBDENABLE);
  RAM #(.addrWidth(7), .clearpin("true"), .dataWidth(7)) ram_1 (
    .addr(ramaddress_1_out_3), .we(and_1_out), .oe(NOTAVAILABLE), .clk(RAMCLK), .din(KDBDATA), .dout(out_1),
    .clr(BTNSIGNALS[0]));
  Clock WRITINGCLOCK (.out(WRITINGCLOCK_out));
  D_Flip_Flop d_ff_1 (.D(1'b1), .clk(BTNSIGNALS[1]), .Q(KBDENABLE), .reset(BTNSIGNALS[0]));  // open: Qn, preset
  or or_3 (RESETROMCOUNTER, BTNSIGNALS[0], BTNSIGNALS[1], BTNSIGNALS[2]);
  Multiplexer multiplexer_1 (.in0(ROMCOUNTERFULLCYCLE), .in1(WRITINGCLOCK_out), .out(RAMCLK), .sel(AVAILABLE));
  and and_2 (and_2_out, NOTAVAILABLE, SHOWMESSAGE);
  or or_4 (or_4_out, AVAILABLE, RESETROMCOUNTER);
  and and_3 (and_3_out, NOTAVAILABLE, clock_2_out);
  Clock clock_2 (.out(clock_2_out));
  D_Flip_Flop d_ff_2 (.D(1'b1), .clk(BTNSIGNALS[2]), .Q(SHOWMESSAGE), .reset(BTNSIGNALS[0]));  // open: Qn, preset
  ContadorA6 contadora6_1 (
    .CLK(and_3_out), .X(and_2_out), .RESET(or_4_out), .out_4(contadora6_1_out_4), .Z(ROMCOUNTERFULLCYCLE));
  RomAddress romaddress_1 (.DIN(out_1), .COUNT(contadora6_1_out_4), .out_3(romaddress_1_out_3));
  ROM #(.addrWidth(10), .dataWidth(7)) rom_1 (.addr(romaddress_1_out_3), .data(rom_1_data));

  // Other names for the same wires on the sheet: OTHERRESETS = BTNSIGNALS[0]; RESETBTNSIGNAL = BTNSIGNALS[0];
  //   RESETKBD = BTNSIGNALS[0]; RESETRAMVALUES = BTNSIGNALS[0]; LOADMESSAGEBTNSIGNAL = BTNSIGNALS[1];
  //   SHOWMESSAGEBTNSIGNAL = BTNSIGNALS[2]

  // Notes on the sheet:
  //   * Limpiar Ram
  //   Señales de los botones
  //   * Limpiar Teclado
  //   * Limpiar Flip Flops
  //   Funcionamiento cuando hacemos click al Reset
  //   Comportamiento del reset de la direccion de la ram
  //   Controlador de reloj de la ram
  //   El reloj de lectura corresponde al flanco de subida generado
  //   por completar un ciclo en el contador de la rom
  //   Comportamiento para resetear el contador de la rom
  //   Funcionamiento cuando iniciamos el cargado del mensaje en la RAM
  //   Funcionamiento cuando iniciamos a mostrar el mensaje en la pantalla
endmodule

module contador (
  input  Cnt,
  output [1:0] out_2
);

  wire and_1_out, and_2_out, and_3_out, CLK, FF0_qn, FF1_qn, not_1_out, or_1_out, xor_1_out;

  Clock u_CLK (.out(CLK));
  not not_1 (not_1_out, Cnt);
  and and_1 (and_1_out, not_1_out, out_2[1]);
  and and_2 (and_2_out, out_2[0], Cnt, FF1_qn);
  and and_3 (and_3_out, Cnt, out_2[1], FF0_qn);
  xor xor_1 (xor_1_out, out_2[0], Cnt);
  or or_1 (or_1_out, and_1_out, and_2_out, and_3_out);
  D_Flip_Flop FF0 (.D(xor_1_out), .clk(CLK), .Q(out_2[0]), .Qn(FF0_qn));  // open: preset, reset
  D_Flip_Flop FF1 (.D(or_1_out), .clk(CLK), .Q(out_2[1]), .Qn(FF1_qn));  // open: preset, reset

  // Other names for the same wires on the sheet: S0 = out_2[0]; S1 = out_2[1]
endmodule

module contador7 (
  input  C,
  input  R,
  output out_3
);

  wire s_r_ff_1_q, s_r_ff_1_qn, s_r_ff_2_q, s_r_ff_2_qn, s_r_ff_3_q, s_r_ff_3_qn;

  S_R_Flip_Flop s_r_ff_1 (
    .S(s_r_ff_1_qn), .R(s_r_ff_1_q), .clk(C), .Q(s_r_ff_1_q), .Qn(s_r_ff_1_qn));  // open: reset, preset
  S_R_Flip_Flop s_r_ff_2 (
    .S(s_r_ff_2_qn), .R(s_r_ff_2_q), .clk(s_r_ff_1_qn), .Q(s_r_ff_2_q), .Qn(s_r_ff_2_qn));  // open: reset, preset
  S_R_Flip_Flop s_r_ff_3 (
    .S(s_r_ff_3_qn), .R(s_r_ff_3_q), .clk(s_r_ff_2_qn), .Q(s_r_ff_3_q), .reset(R), .Qn(s_r_ff_3_qn));  // open: preset
  and and_1 (out_3, s_r_ff_3_q, s_r_ff_2_q, s_r_ff_1_q);
endmodule

module RamAddress (
  input  RESET,
  input  CLK,
  output [6:0] out_3
);

  Counter #(.max('h7f), .width(7)) counter_1 (.clr(RESET), .clk(CLK), .Q(out_3));  // open: load, up, count, D, carry
endmodule

module ResetComp (
  input  AVAILABLE,
  input  CLK,
  input  RESET,
  output ShouldReset
);

  wire d_ff_1_q, d_ff_1_qn, not_1_out, or_1_out, t_ff_1_q;

  not not_1 (not_1_out, AVAILABLE);
  or or_1 (or_1_out, t_ff_1_q, not_1_out);
  T_Flip_Flop t_ff_1 (.T(or_1_out), .clk(CLK), .Q(t_ff_1_q), .reset(RESET));  // open: Qn, preset
  D_Flip_Flop d_ff_1 (.D(t_ff_1_q), .clk(CLK), .Q(d_ff_1_q), .Qn(d_ff_1_qn), .preset(d_ff_1_q), .reset(RESET));
  and and_1 (ShouldReset, t_ff_1_q, d_ff_1_qn);
endmodule

module ContadorA5 (
  input  CLK,
  input  X,
  input  RESET,
  output [2:0] out_4,
  output Z
);

  wire and_1_out, and_2_out, and_3_out, and_4_out, and_5_out, NotQ0, NotQ1, NotQ2, or_1_out;

  and and_1 (and_1_out, X, NotQ1);
  and and_2 (and_2_out, X, NotQ2);
  and and_3 (and_3_out, out_4[0], X, NotQ2);
  and and_4 (and_4_out, X, out_4[0], out_4[1], NotQ2);
  and and_5 (and_5_out, X, out_4[0], NotQ1);
  or or_1 (or_1_out, and_1_out, and_2_out);
  J_K_Flip_Flop j_k_ff_1 (
    .J(or_1_out), .K(or_1_out), .clk(CLK), .Q(out_4[0]), .Qn(NotQ0), .reset(RESET));  // open: preset
  J_K_Flip_Flop j_k_ff_2 (
    .J(and_3_out), .K(and_3_out), .clk(CLK), .Q(out_4[1]), .Qn(NotQ1), .reset(RESET));  // open: preset
  J_K_Flip_Flop j_k_ff_3 (
    .J(and_4_out), .K(and_5_out), .clk(CLK), .Q(out_4[2]), .Qn(NotQ2), .reset(RESET));  // open: preset
  Comparator #(.width(3)) comparator_1 (.a(out_4), .b(3'b101), .eq(Z));  // open: gt, lt

  // Other names for the same wires on the sheet: Q0 = out_4[0]; Q1 = out_4[1]; Q2 = out_4[2]

  // Notes on the sheet:
  //   SALIDA Q0
  //   SALIDA Q1
  //   SALIDA Q2
endmodule

module ten_registers (
  input  [6:0] DIN,
  input  CLK,
  input  RESET,
  output [6:0] DO1,
  output [6:0] DO2,
  output [6:0] DO3,
  output [6:0] DO4,
  output [6:0] DO5,
  output [6:0] DO6,
  output [6:0] DO7,
  output [6:0] DO8,
  output [6:0] DO9,
  output [6:0] DO10
);

  Register #(.width(7)) register_1 (.D(DIN), .clk(CLK), .Q(DO1), .clr(RESET));  // open: en
  Register #(.width(7)) register_2 (.D(DO1), .clk(CLK), .Q(DO2), .clr(RESET));  // open: en
  Register #(.width(7)) register_3 (.D(DO2), .clk(CLK), .Q(DO3), .clr(RESET));  // open: en
  Register #(.width(7)) register_4 (.D(DO3), .clk(CLK), .Q(DO4), .clr(RESET));  // open: en
  Register #(.width(7)) register_5 (.D(DO4), .clk(CLK), .Q(DO5), .clr(RESET));  // open: en
  Register #(.width(7)) register_6 (.D(DO5), .clk(CLK), .Q(DO6), .clr(RESET));  // open: en
  Register #(.width(7)) register_7 (.D(DO6), .clk(CLK), .Q(DO7), .clr(RESET));  // open: en
  Register #(.width(7)) register_8 (.D(DO7), .clk(CLK), .Q(DO8), .clr(RESET));  // open: en
  Register #(.width(7)) register_9 (.D(DO8), .clk(CLK), .Q(DO9), .clr(RESET));  // open: en
  Register #(.width(7)) register_10 (.D(DO9), .clk(CLK), .Q(DO10), .clr(RESET));  // open: en
endmodule

module pantalla (
  input  [6:0] DIN,
  input  RESET
);

  wire clock_1_out;
  wire [6:0] ten_registers_1_do1, ten_registers_1_do2, ten_registers_1_do3, ten_registers_1_do4,
       ten_registers_1_do5, ten_registers_1_do6, ten_registers_1_do7, ten_registers_1_do8,
       ten_registers_1_do9, ten_registers_1_do10, ten_registers_2_do1, ten_registers_2_do2,
       ten_registers_2_do3, ten_registers_2_do4, ten_registers_2_do5, ten_registers_2_do6,
       ten_registers_2_do7, ten_registers_2_do8, ten_registers_2_do9, ten_registers_2_do10,
       ten_registers_3_do1, ten_registers_3_do2, ten_registers_3_do3, ten_registers_3_do4,
       ten_registers_3_do5, ten_registers_3_do6, ten_registers_3_do7, ten_registers_3_do8,
       ten_registers_3_do9, ten_registers_3_do10, ten_registers_4_do1, ten_registers_4_do2,
       ten_registers_4_do3, ten_registers_4_do4, ten_registers_4_do5, ten_registers_4_do6,
       ten_registers_4_do7, ten_registers_4_do8, ten_registers_4_do9, ten_registers_4_do10,
       ten_registers_5_do1, ten_registers_5_do2, ten_registers_5_do3, ten_registers_5_do4,
       ten_registers_5_do5, ten_registers_5_do6, ten_registers_5_do7, ten_registers_5_do8,
       ten_registers_5_do9, ten_registers_5_do10, ten_registers_6_do1, ten_registers_6_do2,
       ten_registers_6_do3, ten_registers_6_do4, ten_registers_6_do5, ten_registers_6_do6,
       ten_registers_6_do7, ten_registers_6_do8, ten_registers_6_do9, ten_registers_6_do10;

  Clock clock_1 (.out(clock_1_out));
  DotMatrix #(.matrixcols(60)) dotmatrix_1 (
    .col0(ten_registers_6_do10), .col1(ten_registers_6_do9), .col2(ten_registers_6_do8),
    .col3(ten_registers_6_do7), .col4(ten_registers_6_do6), .col5(ten_registers_6_do5),
    .col6(ten_registers_6_do4), .col7(ten_registers_6_do3), .col8(ten_registers_6_do2),
    .col9(ten_registers_6_do1), .col10(ten_registers_5_do10), .col11(ten_registers_5_do9),
    .col12(ten_registers_5_do8), .col13(ten_registers_5_do7), .col14(ten_registers_5_do6),
    .col15(ten_registers_5_do5), .col16(ten_registers_5_do4), .col17(ten_registers_5_do3),
    .col18(ten_registers_5_do2), .col19(ten_registers_5_do1), .col20(ten_registers_4_do10),
    .col21(ten_registers_4_do9), .col22(ten_registers_4_do8), .col23(ten_registers_4_do7),
    .col24(ten_registers_4_do6), .col25(ten_registers_4_do5), .col26(ten_registers_4_do4),
    .col27(ten_registers_4_do3), .col28(ten_registers_4_do2), .col29(ten_registers_4_do1),
    .col30(ten_registers_3_do10), .col31(ten_registers_3_do9), .col32(ten_registers_3_do8),
    .col33(ten_registers_3_do7), .col34(ten_registers_3_do6), .col35(ten_registers_3_do5),
    .col36(ten_registers_3_do4), .col37(ten_registers_3_do3), .col38(ten_registers_3_do2),
    .col39(ten_registers_3_do1), .col40(ten_registers_2_do10), .col41(ten_registers_2_do9),
    .col42(ten_registers_2_do8), .col43(ten_registers_2_do7), .col44(ten_registers_2_do6),
    .col45(ten_registers_2_do5), .col46(ten_registers_2_do4), .col47(ten_registers_2_do3),
    .col48(ten_registers_2_do2), .col49(ten_registers_2_do1), .col50(ten_registers_1_do10),
    .col51(ten_registers_1_do9), .col52(ten_registers_1_do8), .col53(ten_registers_1_do7),
    .col54(ten_registers_1_do6), .col55(ten_registers_1_do5), .col56(ten_registers_1_do4),
    .col57(ten_registers_1_do3), .col58(ten_registers_1_do2), .col59(ten_registers_1_do1));
  ten_registers ten_registers_1 (
    .DIN(DIN), .CLK(clock_1_out), .RESET(RESET), .DO1(ten_registers_1_do1), .DO2(ten_registers_1_do2),
    .DO3(ten_registers_1_do3), .DO4(ten_registers_1_do4), .DO5(ten_registers_1_do5),
    .DO6(ten_registers_1_do6), .DO7(ten_registers_1_do7), .DO8(ten_registers_1_do8),
    .DO9(ten_registers_1_do9), .DO10(ten_registers_1_do10));
  ten_registers ten_registers_2 (
    .DIN(ten_registers_1_do10), .CLK(clock_1_out), .RESET(RESET), .DO1(ten_registers_2_do1),
    .DO2(ten_registers_2_do2), .DO3(ten_registers_2_do3), .DO4(ten_registers_2_do4),
    .DO5(ten_registers_2_do5), .DO6(ten_registers_2_do6), .DO7(ten_registers_2_do7),
    .DO8(ten_registers_2_do8), .DO9(ten_registers_2_do9), .DO10(ten_registers_2_do10));
  ten_registers ten_registers_3 (
    .DIN(ten_registers_2_do10), .CLK(clock_1_out), .RESET(RESET), .DO1(ten_registers_3_do1),
    .DO2(ten_registers_3_do2), .DO3(ten_registers_3_do3), .DO4(ten_registers_3_do4),
    .DO5(ten_registers_3_do5), .DO6(ten_registers_3_do6), .DO7(ten_registers_3_do7),
    .DO8(ten_registers_3_do8), .DO9(ten_registers_3_do9), .DO10(ten_registers_3_do10));
  ten_registers ten_registers_4 (
    .DIN(ten_registers_3_do10), .CLK(clock_1_out), .RESET(RESET), .DO1(ten_registers_4_do1),
    .DO2(ten_registers_4_do2), .DO3(ten_registers_4_do3), .DO4(ten_registers_4_do4),
    .DO5(ten_registers_4_do5), .DO6(ten_registers_4_do6), .DO7(ten_registers_4_do7),
    .DO8(ten_registers_4_do8), .DO9(ten_registers_4_do9), .DO10(ten_registers_4_do10));
  ten_registers ten_registers_5 (
    .DIN(ten_registers_4_do10), .CLK(clock_1_out), .RESET(RESET), .DO1(ten_registers_5_do1),
    .DO2(ten_registers_5_do2), .DO3(ten_registers_5_do3), .DO4(ten_registers_5_do4),
    .DO5(ten_registers_5_do5), .DO6(ten_registers_5_do6), .DO7(ten_registers_5_do7),
    .DO8(ten_registers_5_do8), .DO9(ten_registers_5_do9), .DO10(ten_registers_5_do10));
  ten_registers ten_registers_6 (
    .DIN(ten_registers_5_do10), .CLK(clock_1_out), .RESET(RESET), .DO1(ten_registers_6_do1),
    .DO2(ten_registers_6_do2), .DO3(ten_registers_6_do3), .DO4(ten_registers_6_do4),
    .DO5(ten_registers_6_do5), .DO6(ten_registers_6_do6), .DO7(ten_registers_6_do7),
    .DO8(ten_registers_6_do8), .DO9(ten_registers_6_do9), .DO10(ten_registers_6_do10));
endmodule

module ContadorA6 (
  input  CLK,
  input  X,
  input  RESET,
  output [2:0] out_4,
  output Z
);

  wire and_1_out, and_2_out, and_3_out, and_4_out, and_5_out, and_6_out, and_7_out, NotQ0, NotQ1, NotQ2,
       or_1_out, or_2_out;

  and and_1 (and_1_out, NotQ1, X);
  and and_2 (and_2_out, NotQ2, X);
  and and_3 (and_3_out, X, out_4[2]);
  and and_4 (and_4_out, NotQ2, out_4[0], X);
  and and_5 (and_5_out, NotQ1, out_4[0], X);
  and and_6 (and_6_out, X, out_4[0], out_4[1], NotQ2);
  and and_7 (and_7_out, X, out_4[1], NotQ0);
  or or_1 (or_1_out, and_1_out, and_2_out);
  or or_2 (or_2_out, and_3_out, and_4_out);
  J_K_Flip_Flop j_k_ff_1 (
    .J(or_1_out), .K(or_1_out), .clk(CLK), .Q(out_4[0]), .Qn(NotQ0), .reset(RESET));  // open: preset
  J_K_Flip_Flop j_k_ff_2 (
    .J(and_5_out), .K(or_2_out), .clk(CLK), .Q(out_4[1]), .Qn(NotQ1), .reset(RESET));  // open: preset
  J_K_Flip_Flop j_k_ff_3 (
    .J(and_6_out), .K(and_7_out), .clk(CLK), .Q(out_4[2]), .Qn(NotQ2), .reset(RESET));  // open: preset
  Comparator #(.width(3)) comparator_1 (.a(out_4), .b(3'b110), .eq(Z));  // open: gt, lt

  // Other names for the same wires on the sheet: Q0 = out_4[0]; Q1 = out_4[1]; Q2 = out_4[2]

  // Notes on the sheet:
  //   SALIDA Q1
  //   SALIDA Q2
endmodule

module RamCirc (
  input  RESET,
  input  WRITE,
  input  CLK,
  input  READ,
  input  [6:0] DATAINPUT,
  output [6:0] DATAOUT
);

  wire [6:0] ramaddress_1_out_3;

  RamAddress ramaddress_1 (.RESET(RESET), .CLK(CLK), .out_3(ramaddress_1_out_3));
  RAM #(.addrWidth(7), .dataWidth(7)) ram_1 (
    .addr(ramaddress_1_out_3), .we(WRITE), .oe(READ), .clk(CLK), .din(DATAINPUT), .dout(DATAOUT));
endmodule

module Circuito (
  input  RESET,
  input  AVAILABLE,
  input  [6:0] DATAINPUT,
  output [6:0] COLUMNDISPLAY
);

  wire clock_1_out, clockswitcher_1_clk, contadora5_1_z, not_1_out, not_2_out, resetcomp_1_shouldreset;
  wire [2:0] contadora5_1_out_4;
  wire [6:0] ramcirc_1_dataout;

  Clock clock_1 (.out(clock_1_out));
  not not_1 (not_1_out, AVAILABLE);
  ClOCKSWITCHER clockswitcher_1 (.AVAILABLE(AVAILABLE), .Z(contadora5_1_z), .CLK(clockswitcher_1_clk));
  ContadorA5 contadora5_1 (
    .CLK(clock_1_out), .X(not_1_out), .RESET(RESET), .out_4(contadora5_1_out_4), .Z(contadora5_1_z));
  not not_2 (not_2_out, AVAILABLE);
  ResetComp resetcomp_1 (
    .AVAILABLE(AVAILABLE), .CLK(clockswitcher_1_clk), .RESET(RESET), .ShouldReset(resetcomp_1_shouldreset));
  RamCirc ramcirc_1 (
    .RESET(resetcomp_1_shouldreset), .WRITE(AVAILABLE), .CLK(clockswitcher_1_clk), .READ(not_2_out),
    .DATAINPUT(DATAINPUT), .DATAOUT(ramcirc_1_dataout));
  RomCirc romcirc_1 (.RAMVALUE(ramcirc_1_dataout), .COUNTVALUE(contadora5_1_out_4), .COLUMDISPLAY(COLUMNDISPLAY));
endmodule

module RomCirc (
  input  [6:0] RAMVALUE,
  input  [2:0] COUNTVALUE,
  output [6:0] COLUMDISPLAY
);

  wire [6:0] adder_1_out, multiplier_1_out, subtractor_1_out;

  Subtractor #(.width(7)) subtractor_1 (.a(RAMVALUE), .b(7'b0100000), .out(subtractor_1_out));  // open: bin, bout
  Multiplier #(.width(7)) multiplier_1 (
    .a(subtractor_1_out), .b(7'b0000110), .out(multiplier_1_out));  // open: cin, cout
  Adder #(.width(7)) adder_1 (.a(multiplier_1_out), .b({4'b0000, COUNTVALUE}), .out(adder_1_out));  // open: cin, cout
  ROM #(.addrWidth(10), .dataWidth(7)) rom_1 (.addr({3'b000, adder_1_out}), .data(COLUMDISPLAY));
endmodule

module ClOCKSWITCHER (
  input  AVAILABLE,
  input  Z,
  output CLK
);

  wire clock_1_out;

  Clock clock_1 (.out(clock_1_out));
  Multiplexer multiplexer_1 (.in0(Z), .in1(clock_1_out), .out(CLK), .sel(AVAILABLE));
endmodule

module LatchSR (
  input  R,
  input  S,
  output Q,
  output NotQ
);

  nor nor_1 (Q, R, NotQ);
  nor nor_2 (NotQ, Q, S);
endmodule

module convert1To7 (
  input  DIN,
  output [6:0] DOUT
);


  assign DOUT = {{6{1'b0}}, DIN};
endmodule

module RomAddress (
  input  [6:0] DIN,
  input  [2:0] COUNT,
  output [9:0] out_3
);

  wire comparator_1_eq;
  wire [6:0] multiplexer_1_out, multiplier_1_out, subtractor_1_out;

  Comparator #(.width(7)) comparator_1 (.a(DIN), .b({7{1'b0}}), .eq(comparator_1_eq));  // open: gt, lt
  Multiplexer #(.width(7)) multiplexer_1 (.in0(DIN), .in1(7'b0100000), .out(multiplexer_1_out), .sel(comparator_1_eq));
  Subtractor #(.width(7)) subtractor_1 (
    .a(multiplexer_1_out), .b(7'b0100000), .out(subtractor_1_out));  // open: bin, bout
  Multiplier #(.width(7)) multiplier_1 (
    .a(subtractor_1_out), .b(7'b0000110), .out(multiplier_1_out));  // open: cin, cout
  Adder #(.width(7)) adder_1 (.a(multiplier_1_out), .b({4'b0000, COUNT}), .out(out_3[6:0]));  // open: cin, cout

  assign out_3[9:7] = 3'b000;
endmodule
